# Fritzing sketch Sound_Detector (saved by Fritzing 1.0.4)
breadboards: 1

parts:
  A1 = ESP32-C6-DevKitC-1
  SW1 = DIP SWITCH [package=dipswitch-02]
  LED1 = RGB LED (com. cathode, rgb) [color="Red (633nm)" current=0.030A package="5 mm [THT]"]
  R1 = Resistor [tolerance=±5% power=0.25W resistance=330 package=THT]
  R2 = Resistor [tolerance=±5% power=0.25W resistance=330 package=THT]
  R3 = Resistor [tolerance=±5% power=0.25W resistance=330 package=THT]
  Part1 = INMP441
  SP1 = SPEAKER [package=pcb_mount_speaker]
  R4 = Resistor [tolerance=±5% power=0.25W resistance=330 package=THT]
  Q1 = NPN-Transistor [part_number="JC2N 3904" package="TO92 [THT]"]

nets:
  N1: A1.Pin_1, Part1.L/R, Part1.VDD, SP1.-
  N2: A1.Pin_3, Part1.SD
  N3: A1.Pin_4, Part1.SCK
  N4: A1.Pin_5, Part1.WS
  N5: A1.Pin_8, SW1.1
  N6: A1.Pin_15, A1.Pin_18, A1.Pin_32, LED1.common_cathode, Part1.GND, Q1.C
  N7: A1.Pin_24, R3.Pin_1
  N8: A1.Pin_25, R1.Pin_1
  N9: A1.Pin_26, R2.Pin_1
  N10: SW1.4, R4.Pin_0
  N11: LED1.red_anode, R3.Pin_0
  N12: LED1.green_anode, R2.Pin_0
  N13: LED1.blue_anode, R1.Pin_0
  N14: SP1.+, Q1.E
  N15: R4.Pin_1, Q1.B

custom parts:
  ESP32-C6-DevKitC-1: ESP32-C6-DevKitC-1 is an entry-level development board based on ESP32-C6-WROOM-1(U), a general-purpose module with a 8 MB SPI flash. This board integrates complete Wi-Fi, Bluetooth LE, Zigbee, and Thread functions.
  INMP441: This is a simple breakout board for the INMP441 I2S MEMS microphone.
